# Fritzing sketch LED1 (saved by Fritzing 0.9.2b)
breadboards: 1

parts:
  Raspberry_Pi_3 = Raspberry Pi 2
  S1 = Pushbutton [package="[THT]"]
  R1 = Resistor [tolerance=±5% resistance=220 package=THT]
  LED1 = LED - 5mm [color="Red (633nm)" package="5 mm [THT]"]

nets:
  N1: Raspberry_Pi_3.GPIO17, R1.Pin_0
  N2: Raspberry_Pi_3.GND, S1.Pin_1, S1.Pin_2, LED1.cathode
  N3: Raspberry_Pi_3.GPIO26, S1.Pin_3, S1.Pin_4
  N4: R1.Pin_1, LED1.anode
